# Fritzing sketch LED_Schaltung 2024-11-20 (saved by Fritzing 1.0.0rc)
circuit board: 7.92cm x 4.6cm
breadboards: 1

parts:
  LED = LED - 5mm [color="Red (633nm)" current=0.030A package="5 mm [THT]"]
  9V_Batterie = Battery block 9V  # not connected
  Drucktaster = Pushbutton [package="[THT]"]
  Widerstand_330_Ohm = Resistor [tolerance=±5% power=0.25W resistance=330 package=THT]
  9V = Screw terminal - 2 pins [package=THT]

nets:
  N1: LED.cathode, Drucktaster.Pin_3, Drucktaster.Pin_4
  N2: LED.anode, Widerstand_330_Ohm.Pin_1
  N3: Drucktaster.Pin_1, Drucktaster.Pin_2, 9V.pin2
  N4: Widerstand_330_Ohm.Pin_0, 9V.pin1

notes:
  LED Schaltung
  -
  +
  ver.2024-11-20 by DM9GP
  GND
  Rot
  '
